// Logisim project 8bit_ALU.circ as structural Verilog: 1 circuit, main circuit 8bit_ALU
// ALU
module _8bit_ALU (
  input  A7,
  input  A6,
  input  A5,
  input  A4,
  input  A3,
  input  A2,
  input  A1,
  input  A0,
  input  S1,
  input  S0,
  input  B7,
  input  B6,
  input  B5,
  input  B4,
  input  B3,
  input  B2,
  input  B1,
  input  B0,
  output O0,
  output O1,
  output O2,
  output O3,
  output O4,
  output O5,
  output O6,
  output O7
);

  wire n8bit_adder_subtractor_1_o0, n8bit_adder_subtractor_1_o1, n8bit_adder_subtractor_1_o2,
       n8bit_adder_subtractor_1_o3, n8bit_adder_subtractor_1_o4, n8bit_adder_subtractor_1_o5,
       n8bit_adder_subtractor_1_o6, n8bit_adder_subtractor_1_o7, n8bit_and_1_o0, n8bit_and_1_o1,
       n8bit_and_1_o2, n8bit_and_1_o3, n8bit_and_1_o4, n8bit_and_1_o5, n8bit_and_1_o6, n8bit_and_1_o7,
       n8bit_or_1_o0, n8bit_or_1_o1, n8bit_or_1_o2, n8bit_or_1_o3, n8bit_or_1_o4, n8bit_or_1_o5,
       n8bit_or_1_o6, n8bit_or_1_o7;

  _8bit_and u_8bit_and_1 (
    .O1(n8bit_and_1_o1), .O0(n8bit_and_1_o0), .O2(n8bit_and_1_o2), .O3(n8bit_and_1_o3), .O4(n8bit_and_1_o4),
    .O5(n8bit_and_1_o5), .O6(n8bit_and_1_o6), .O7(n8bit_and_1_o7), .A0(A0), .A1(A1), .A2(A2), .A3(A3),
    .A4(A4), .A5(A5), .A6(A6), .A7(A7), .B7(B7), .B6(B6), .B5(B5), .B4(B4), .B3(B3), .B2(B2), .B1(B1), .B0(B0));
  _8bit_or u_8bit_or_1 (
    .O1(n8bit_or_1_o1), .O0(n8bit_or_1_o0), .O2(n8bit_or_1_o2), .O3(n8bit_or_1_o3), .O4(n8bit_or_1_o4),
    .O5(n8bit_or_1_o5), .O6(n8bit_or_1_o6), .O7(n8bit_or_1_o7), .A0(A0), .A1(A1), .A2(A2), .A3(A3), .A4(A4),
    .A5(A5), .A6(A6), .A7(A7), .B7(B7), .B6(B6), .B5(B5), .B4(B4), .B3(B3), .B2(B2), .B1(B1), .B0(B0));
  _8bit_adder_subtractor u_8bit_adder_subtractor_1 (
    .S0(S0), .Y7(B7), .Y6(B6), .Y5(B5), .Y4(B4), .Y3(B3), .Y2(B2), .Y1(B1), .Y0(B0), .X7(A7), .X6(A6),
    .X5(A5), .X4(A4), .X3(A3), .X2(A2), .X1(A1), .X0(A0), .O0(n8bit_adder_subtractor_1_o0),
    .O1(n8bit_adder_subtractor_1_o1), .O2(n8bit_adder_subtractor_1_o2), .O3(n8bit_adder_subtractor_1_o3),
    .O4(n8bit_adder_subtractor_1_o4), .O5(n8bit_adder_subtractor_1_o5), .O6(n8bit_adder_subtractor_1_o6),
    .O7(n8bit_adder_subtractor_1_o7));
  _8bit_multiplexor_2 u_8bit_multiplexor_2_1 (
    .S1(S1), .O0(O0), .O1(O1), .O2(O2), .O3(O3), .O4(O4), .O5(O5), .O6(O6), .O7(O7), .A7(n8bit_and_1_o7),
    .A6(n8bit_and_1_o6), .A5(n8bit_and_1_o5), .A4(n8bit_and_1_o4), .A3(n8bit_and_1_o3), .A2(n8bit_and_1_o2),
    .A1(n8bit_and_1_o1), .A0(n8bit_and_1_o0), .B7(n8bit_or_1_o7), .B6(n8bit_or_1_o6), .B5(n8bit_or_1_o5),
    .B4(n8bit_or_1_o4), .B3(n8bit_or_1_o3), .B2(n8bit_or_1_o2), .B1(n8bit_or_1_o1), .B0(n8bit_or_1_o0),
    .S0(S0), .C7(n8bit_adder_subtractor_1_o7), .C6(n8bit_adder_subtractor_1_o6),
    .C5(n8bit_adder_subtractor_1_o5), .C4(n8bit_adder_subtractor_1_o4), .C3(n8bit_adder_subtractor_1_o3),
    .C2(n8bit_adder_subtractor_1_o2), .C1(n8bit_adder_subtractor_1_o1), .C0(n8bit_adder_subtractor_1_o0));  // open: D7, D6, D5, D4, D3, D2, D1, D0
endmodule
