// Logisim project 8bit_adder.circ as structural Verilog: 1 circuit, main circuit 8bit_adder
// ADD
module _8bit_adder (
  input  X7,
  input  X6,
  input  X5,
  input  X4,
  input  X3,
  input  X2,
  input  X1,
  input  X0,
  input  Y7,
  input  Y6,
  input  Y5,
  input  Y4,
  input  Y3,
  input  Y2,
  input  Y1,
  input  Y0,
  output O0,
  output O1,
  output O2,
  output O3,
  output O4,
  output O5,
  output O6,
  output O7,
  output S0
);

  wire full_adder_1_co0, full_adder_2_co0, full_adder_3_co0, full_adder_4_co0, full_adder_5_co0,
       full_adder_6_co0, full_adder_7_co0;

  full_adder full_adder_1 (.X0(X0), .Y0(Y0), .Ci0(1'b0), .O0(O0), .Co0(full_adder_1_co0));
  full_adder full_adder_2 (.X0(X1), .Y0(Y1), .Ci0(full_adder_1_co0), .O0(O1), .Co0(full_adder_2_co0));
  full_adder full_adder_3 (.X0(X2), .Y0(Y2), .Ci0(full_adder_2_co0), .O0(O2), .Co0(full_adder_3_co0));
  full_adder full_adder_4 (.X0(X3), .Y0(Y3), .Ci0(full_adder_3_co0), .O0(O3), .Co0(full_adder_4_co0));
  full_adder full_adder_5 (.X0(X4), .Y0(Y4), .Ci0(full_adder_4_co0), .O0(O4), .Co0(full_adder_5_co0));
  full_adder full_adder_6 (.X0(X5), .Y0(Y5), .Ci0(full_adder_5_co0), .O0(O5), .Co0(full_adder_6_co0));
  full_adder full_adder_7 (.X0(X6), .Y0(Y6), .Ci0(full_adder_6_co0), .O0(O6), .Co0(full_adder_7_co0));
  full_adder full_adder_8 (.X0(X7), .Y0(Y7), .Ci0(full_adder_7_co0), .O0(O7), .Co0(S0));
endmodule
