// Logisim project 8bit_adder_subtractor.circ as structural Verilog: 1 circuit, main circuit 8bit_adder_subtractor
// ADD-SUB
module _8bit_adder_subtractor (
  input  X7,
  input  X6,
  input  X5,
  input  X4,
  input  X3,
  input  X2,
  input  X1,
  input  X0,
  input  S0,
  input  Y7,
  input  Y6,
  input  Y5,
  input  Y4,
  input  Y3,
  input  Y2,
  input  Y1,
  input  Y0,
  output O0,
  output O1,
  output O2,
  output O3,
  output O4,
  output O5,
  output O6,
  output O7
);

  wire n8bit_adder_1_o0, n8bit_adder_1_o1, n8bit_adder_1_o2, n8bit_adder_1_o3, n8bit_adder_1_o4,
       n8bit_adder_1_o5, n8bit_adder_1_o6, n8bit_adder_1_o7, n8bit_multiplexor_1_1_o0,
       n8bit_multiplexor_1_1_o1, n8bit_multiplexor_1_1_o2, n8bit_multiplexor_1_1_o3,
       n8bit_multiplexor_1_1_o4, n8bit_multiplexor_1_1_o5, n8bit_multiplexor_1_1_o6,
       n8bit_multiplexor_1_1_o7, n8bit_multiplexor_1_2_o0, n8bit_multiplexor_1_2_o1,
       n8bit_multiplexor_1_2_o2, n8bit_multiplexor_1_2_o3, n8bit_multiplexor_1_2_o4,
       n8bit_multiplexor_1_2_o5, n8bit_multiplexor_1_2_o6, n8bit_multiplexor_1_2_o7, xor_1_out, xor_2_out,
       xor_3_out, xor_4_out, xor_5_out, xor_6_out, xor_7_out, xor_8_out;

  _8bit_multiplexor_1 u_8bit_multiplexor_1_1 (
    .S0(S0), .O0(n8bit_multiplexor_1_1_o0), .O1(n8bit_multiplexor_1_1_o1), .O2(n8bit_multiplexor_1_1_o2),
    .O3(n8bit_multiplexor_1_1_o3), .O4(n8bit_multiplexor_1_1_o4), .O5(n8bit_multiplexor_1_1_o5),
    .O6(n8bit_multiplexor_1_1_o6), .O7(n8bit_multiplexor_1_1_o7), .A7(1'b0), .A6(1'b0), .A5(1'b0), .A4(1'b0),
    .A3(1'b0), .A2(1'b0), .A1(1'b0), .A0(1'b0), .B7(1'b1), .B6(1'b1), .B5(1'b1), .B4(1'b1), .B3(1'b1),
    .B2(1'b1), .B1(1'b1), .B0(1'b1));
  xor xor_1 (xor_1_out, n8bit_multiplexor_1_1_o0, Y0);
  xor xor_2 (xor_2_out, n8bit_multiplexor_1_1_o1, Y1);
  xor xor_3 (xor_3_out, n8bit_multiplexor_1_1_o2, Y2);
  xor xor_4 (xor_4_out, n8bit_multiplexor_1_1_o3, Y3);
  xor xor_5 (xor_5_out, n8bit_multiplexor_1_1_o4, Y4);
  xor xor_6 (xor_6_out, n8bit_multiplexor_1_1_o5, Y5);
  xor xor_7 (xor_7_out, n8bit_multiplexor_1_1_o6, Y6);
  xor xor_8 (xor_8_out, n8bit_multiplexor_1_1_o7, Y7);
  _8bit_multiplexor_1 u_8bit_multiplexor_1_2 (
    .S0(S0), .O0(n8bit_multiplexor_1_2_o0), .O1(n8bit_multiplexor_1_2_o1), .O2(n8bit_multiplexor_1_2_o2),
    .O3(n8bit_multiplexor_1_2_o3), .O4(n8bit_multiplexor_1_2_o4), .O5(n8bit_multiplexor_1_2_o5),
    .O6(n8bit_multiplexor_1_2_o6), .O7(n8bit_multiplexor_1_2_o7), .A7(1'b0), .A6(1'b0), .A5(1'b0), .A4(1'b0),
    .A3(1'b0), .A2(1'b0), .A1(1'b0), .A0(1'b0), .B7(1'b0), .B6(1'b0), .B5(1'b0), .B4(1'b0), .B3(1'b0),
    .B2(1'b0), .B1(1'b0), .B0(1'b1));
  _8bit_adder u_8bit_adder_1 (
    .X0(xor_1_out), .X2(xor_3_out), .X3(xor_4_out), .X4(xor_5_out), .X5(xor_6_out), .X6(xor_7_out),
    .X7(xor_8_out), .Y7(n8bit_multiplexor_1_2_o7), .Y6(n8bit_multiplexor_1_2_o6),
    .Y5(n8bit_multiplexor_1_2_o5), .Y4(n8bit_multiplexor_1_2_o4), .Y3(n8bit_multiplexor_1_2_o3),
    .Y2(n8bit_multiplexor_1_2_o2), .Y1(n8bit_multiplexor_1_2_o1), .Y0(n8bit_multiplexor_1_2_o0),
    .O7(n8bit_adder_1_o7), .O6(n8bit_adder_1_o6), .O5(n8bit_adder_1_o5), .O4(n8bit_adder_1_o4),
    .O3(n8bit_adder_1_o3), .O2(n8bit_adder_1_o2), .O1(n8bit_adder_1_o1), .O0(n8bit_adder_1_o0), .X1(xor_2_out));
  _8bit_adder u_8bit_adder_2 (
    .X0(X0), .X2(X2), .X3(X3), .X4(X4), .X5(X5), .X6(X6), .X7(X7), .Y7(n8bit_adder_1_o7),
    .Y6(n8bit_adder_1_o6), .Y5(n8bit_adder_1_o5), .Y4(n8bit_adder_1_o4), .Y3(n8bit_adder_1_o3),
    .Y2(n8bit_adder_1_o2), .Y1(n8bit_adder_1_o1), .Y0(n8bit_adder_1_o0), .O7(O7), .O6(O6), .O5(O5), .O4(O4),
    .O3(O3), .O2(O2), .O1(O1), .O0(O0), .X1(X1));
endmodule
