// Logisim project 8bit_and.circ as structural Verilog: 1 circuit, main circuit 8bit_and
// AND
module _8bit_and (
  input  A7,
  input  A6,
  input  A5,
  input  A4,
  input  A3,
  input  A2,
  input  A1,
  input  A0,
  input  B7,
  input  B6,
  input  B5,
  input  B4,
  input  B3,
  input  B2,
  input  B1,
  input  B0,
  output O0,
  output O1,
  output O2,
  output O3,
  output O4,
  output O5,
  output O6,
  output O7
);

  and and_1 (O0, A0, B0);
  and and_2 (O1, A1, B1);
  and and_3 (O2, A2, B2);
  and and_4 (O3, A3, B3);
  and and_5 (O4, A4, B4);
  and and_6 (O5, A5, B5);
  and and_7 (O6, A6, B6);
  and and_8 (O7, A7, B7);
endmodule
