// Logisim project 8bit_multiplexor_1.circ as structural Verilog: 1 circuit, main circuit 8bit_multiplexor_1
// MUX
module _8bit_multiplexor_1 (
  input  A7,
  input  A6,
  input  A5,
  input  A4,
  input  A3,
  input  A2,
  input  A1,
  input  A0,
  input  S0,
  input  B7,
  input  B6,
  input  B5,
  input  B4,
  input  B3,
  input  B2,
  input  B1,
  input  B0,
  output O0,
  output O1,
  output O2,
  output O3,
  output O4,
  output O5,
  output O6,
  output O7
);

  wire and_1_out, and_2_out, and_3_out, and_4_out, and_5_out, and_6_out, and_7_out, and_8_out, and_9_out,
       and_10_out, and_11_out, and_12_out, and_13_out, and_14_out, and_15_out, and_16_out, not_1_out;

  not not_1 (not_1_out, S0);
  and and_1 (and_1_out, A0, not_1_out);
  and and_2 (and_2_out, S0, B0);
  and and_3 (and_3_out, A1, not_1_out);
  and and_4 (and_4_out, S0, B1);
  and and_5 (and_5_out, A2, not_1_out);
  and and_6 (and_6_out, S0, B2);
  and and_7 (and_7_out, A3, not_1_out);
  and and_8 (and_8_out, S0, B3);
  and and_9 (and_9_out, A4, not_1_out);
  and and_10 (and_10_out, S0, B4);
  and and_11 (and_11_out, A5, not_1_out);
  and and_12 (and_12_out, S0, B5);
  and and_13 (and_13_out, A6, not_1_out);
  and and_14 (and_14_out, S0, B6);
  and and_15 (and_15_out, A7, not_1_out);
  _8bit_or u_8bit_or_1 (
    .O1(O1), .O0(O0), .O2(O2), .O3(O3), .O4(O4), .O5(O5), .O6(O6), .O7(O7), .A0(and_1_out), .A1(and_3_out),
    .A2(and_5_out), .A3(and_7_out), .A4(and_9_out), .A5(and_11_out), .A6(and_13_out), .A7(and_15_out),
    .B7(and_16_out), .B6(and_14_out), .B5(and_12_out), .B4(and_10_out), .B3(and_8_out), .B2(and_6_out),
    .B1(and_4_out), .B0(and_2_out));
  and and_16 (and_16_out, S0, B7);
endmodule
