// Logisim project 8bit_multiplexor_2.circ as structural Verilog: 1 circuit, main circuit 8bit_multiplexor_2
// MUX
module _8bit_multiplexor_2 (
  input  A7,
  input  A6,
  input  A5,
  input  A4,
  input  A3,
  input  A2,
  input  A1,
  input  A0,
  input  B7,
  input  B6,
  input  B5,
  input  B4,
  input  B3,
  input  B2,
  input  B1,
  input  B0,
  input  S1,
  input  S0,
  input  C7,
  input  C6,
  input  C5,
  input  C4,
  input  C3,
  input  C2,
  input  C1,
  input  C0,
  input  D7,
  input  D6,
  input  D5,
  input  D4,
  input  D3,
  input  D2,
  input  D1,
  input  D0,
  output O0,
  output O1,
  output O2,
  output O3,
  output O4,
  output O5,
  output O6,
  output O7
);

  wire and_1_out, and_2_out, and_3_out, and_4_out, and_5_out, and_6_out, and_7_out, and_8_out, and_9_out,
       and_10_out, and_11_out, and_12_out, and_13_out, and_14_out, and_15_out, and_16_out, and_17_out,
       and_18_out, and_19_out, and_20_out, and_21_out, and_22_out, and_23_out, and_24_out, and_25_out,
       and_26_out, and_27_out, and_28_out, and_29_out, and_30_out, and_31_out, and_32_out, n8bit_or_1_o0,
       n8bit_or_1_o1, n8bit_or_1_o2, n8bit_or_1_o3, n8bit_or_1_o4, n8bit_or_1_o5, n8bit_or_1_o6,
       n8bit_or_1_o7, n8bit_or_2_o0, n8bit_or_2_o1, n8bit_or_2_o2, n8bit_or_2_o3, n8bit_or_2_o4,
       n8bit_or_2_o5, n8bit_or_2_o6, n8bit_or_2_o7, not_1_out, not_2_out;

  not not_1 (not_1_out, S1);
  not not_2 (not_2_out, S0);
  and and_1 (and_1_out, A0, not_2_out, not_1_out);
  and and_2 (and_2_out, S1, not_2_out, C0);
  and and_3 (and_3_out, A1, not_2_out, not_1_out);
  and and_4 (and_4_out, S1, not_2_out, C1);
  and and_5 (and_5_out, A2, not_2_out, not_1_out);
  and and_6 (and_6_out, S1, not_2_out, C2);
  and and_7 (and_7_out, A3, not_2_out, not_1_out);
  and and_8 (and_8_out, S1, not_2_out, C3);
  and and_9 (and_9_out, A4, not_2_out, not_1_out);
  and and_10 (and_10_out, S1, not_2_out, C4);
  and and_11 (and_11_out, A5, not_2_out, not_1_out);
  and and_12 (and_12_out, S1, not_2_out, C5);
  and and_13 (and_13_out, A6, not_2_out, not_1_out);
  and and_14 (and_14_out, S1, not_2_out, C6);
  and and_15 (and_15_out, A7, not_2_out, not_1_out);
  and and_16 (and_16_out, S1, not_2_out, C7);
  and and_17 (and_17_out, B0, S0, not_1_out);
  and and_18 (and_18_out, S1, S0, D0);
  and and_19 (and_19_out, B1, S0, not_1_out);
  and and_20 (and_20_out, S1, S0, D1);
  and and_21 (and_21_out, B2, S0, not_1_out);
  and and_22 (and_22_out, S1, S0, D2);
  and and_23 (and_23_out, B3, S0, not_1_out);
  and and_24 (and_24_out, S1, S0, D3);
  and and_25 (and_25_out, B4, S0, not_1_out);
  and and_26 (and_26_out, S1, S0, D4);
  and and_27 (and_27_out, B5, S0, not_1_out);
  and and_28 (and_28_out, S1, S0, D5);
  and and_29 (and_29_out, B6, S0, not_1_out);
  and and_30 (and_30_out, S1, S0, D6);
  and and_31 (and_31_out, B7, S0, not_1_out);
  and and_32 (and_32_out, S1, S0, D7);
  _8bit_or u_8bit_or_1 (
    .O1(n8bit_or_1_o1), .O0(n8bit_or_1_o0), .O2(n8bit_or_1_o2), .O3(n8bit_or_1_o3), .O4(n8bit_or_1_o4),
    .O5(n8bit_or_1_o5), .O6(n8bit_or_1_o6), .O7(n8bit_or_1_o7), .A0(and_1_out), .A1(and_3_out),
    .A2(and_5_out), .A3(and_7_out), .A4(and_9_out), .A5(and_11_out), .A6(and_13_out), .A7(and_15_out),
    .B7(and_31_out), .B6(and_29_out), .B5(and_27_out), .B4(and_25_out), .B3(and_23_out), .B2(and_21_out),
    .B1(and_19_out), .B0(and_17_out));
  _8bit_or u_8bit_or_2 (
    .O1(n8bit_or_2_o1), .O0(n8bit_or_2_o0), .O2(n8bit_or_2_o2), .O3(n8bit_or_2_o3), .O4(n8bit_or_2_o4),
    .O5(n8bit_or_2_o5), .O6(n8bit_or_2_o6), .O7(n8bit_or_2_o7), .A0(and_18_out), .A1(and_20_out),
    .A2(and_22_out), .A3(and_24_out), .A4(and_26_out), .A5(and_28_out), .A6(and_30_out), .A7(and_32_out),
    .B7(and_16_out), .B6(and_14_out), .B5(and_12_out), .B4(and_10_out), .B3(and_8_out), .B2(and_6_out),
    .B1(and_4_out), .B0(and_2_out));
  _8bit_or u_8bit_or_3 (
    .O1(O1), .O0(O0), .O2(O2), .O3(O3), .O4(O4), .O5(O5), .O6(O6), .O7(O7), .A0(n8bit_or_1_o0),
    .A1(n8bit_or_1_o1), .A2(n8bit_or_1_o2), .A3(n8bit_or_1_o3), .A4(n8bit_or_1_o4), .A5(n8bit_or_1_o5),
    .A6(n8bit_or_1_o6), .A7(n8bit_or_1_o7), .B7(n8bit_or_2_o7), .B6(n8bit_or_2_o6), .B5(n8bit_or_2_o5),
    .B4(n8bit_or_2_o4), .B3(n8bit_or_2_o3), .B2(n8bit_or_2_o2), .B1(n8bit_or_2_o1), .B0(n8bit_or_2_o0));
endmodule
