// Logisim project adder_subtractor.circ as structural Verilog: 1 circuit, main circuit adder_subtractor
// ADD-SUB
module adder_subtractor (
  input  X7,
  input  X6,
  input  X5,
  input  X4,
  input  X3,
  input  X2,
  input  X1,
  input  X0,
  input  S0,
  input  Y7,
  input  Y6,
  input  Y5,
  input  Y4,
  input  Y3,
  input  Y2,
  input  Y1,
  input  Y0,
  output O0,
  output O1,
  output O2,
  output O3,
  output O4,
  output O5,
  output O6,
  output O7
);

  wire adder_1_o0, adder_1_o1, adder_1_o2, adder_1_o3, adder_1_o4, adder_1_o5, adder_1_o6, adder_1_o7,
       multiplexor_1_1_o0, multiplexor_1_1_o1, multiplexor_1_1_o2, multiplexor_1_1_o3, multiplexor_1_1_o4,
       multiplexor_1_1_o5, multiplexor_1_1_o6, multiplexor_1_1_o7, multiplexor_1_2_o0, multiplexor_1_2_o1,
       multiplexor_1_2_o2, multiplexor_1_2_o3, multiplexor_1_2_o4, multiplexor_1_2_o5, multiplexor_1_2_o6,
       multiplexor_1_2_o7, xor_1_out, xor_2_out, xor_3_out, xor_4_out, xor_5_out, xor_6_out, xor_7_out,
       xor_8_out;

  multiplexor_1 multiplexor_1_1 (
    .S0(S0), .O0(multiplexor_1_1_o0), .O1(multiplexor_1_1_o1), .O2(multiplexor_1_1_o2),
    .O3(multiplexor_1_1_o3), .O4(multiplexor_1_1_o4), .O5(multiplexor_1_1_o5), .O6(multiplexor_1_1_o6),
    .O7(multiplexor_1_1_o7), .A7(1'b0), .A6(1'b0), .A5(1'b0), .A4(1'b0), .A3(1'b0), .A2(1'b0), .A1(1'b0),
    .A0(1'b0), .B7(1'b1), .B6(1'b1), .B5(1'b1), .B4(1'b1), .B3(1'b1), .B2(1'b1), .B1(1'b1), .B0(1'b1));
  xor xor_1 (xor_1_out, multiplexor_1_1_o0, Y0);
  xor xor_2 (xor_2_out, multiplexor_1_1_o1, Y1);
  xor xor_3 (xor_3_out, multiplexor_1_1_o2, Y2);
  xor xor_4 (xor_4_out, multiplexor_1_1_o3, Y3);
  xor xor_5 (xor_5_out, multiplexor_1_1_o4, Y4);
  xor xor_6 (xor_6_out, multiplexor_1_1_o5, Y5);
  xor xor_7 (xor_7_out, multiplexor_1_1_o6, Y6);
  xor xor_8 (xor_8_out, multiplexor_1_1_o7, Y7);
  multiplexor_1 multiplexor_1_2 (
    .S0(S0), .O0(multiplexor_1_2_o0), .O1(multiplexor_1_2_o1), .O2(multiplexor_1_2_o2),
    .O3(multiplexor_1_2_o3), .O4(multiplexor_1_2_o4), .O5(multiplexor_1_2_o5), .O6(multiplexor_1_2_o6),
    .O7(multiplexor_1_2_o7), .A7(1'b0), .A6(1'b0), .A5(1'b0), .A4(1'b0), .A3(1'b0), .A2(1'b0), .A1(1'b0),
    .A0(1'b0), .B7(1'b0), .B6(1'b0), .B5(1'b0), .B4(1'b0), .B3(1'b0), .B2(1'b0), .B1(1'b0), .B0(1'b1));
  adder adder_1 (
    .X0(xor_1_out), .X2(xor_3_out), .X3(xor_4_out), .X4(xor_5_out), .X5(xor_6_out), .X6(xor_7_out),
    .X7(xor_8_out), .Y7(multiplexor_1_2_o7), .Y6(multiplexor_1_2_o6), .Y5(multiplexor_1_2_o5),
    .Y4(multiplexor_1_2_o4), .Y3(multiplexor_1_2_o3), .Y2(multiplexor_1_2_o2), .Y1(multiplexor_1_2_o1),
    .Y0(multiplexor_1_2_o0), .O7(adder_1_o7), .O6(adder_1_o6), .O5(adder_1_o5), .O4(adder_1_o4),
    .O3(adder_1_o3), .O2(adder_1_o2), .O1(adder_1_o1), .O0(adder_1_o0), .X1(xor_2_out));
  adder adder_2 (
    .X0(X0), .X2(X2), .X3(X3), .X4(X4), .X5(X5), .X6(X6), .X7(X7), .Y7(adder_1_o7), .Y6(adder_1_o6),
    .Y5(adder_1_o5), .Y4(adder_1_o4), .Y3(adder_1_o3), .Y2(adder_1_o2), .Y1(adder_1_o1), .Y0(adder_1_o0),
    .O7(O7), .O6(O6), .O5(O5), .O4(O4), .O3(O3), .O2(O2), .O1(O1), .O0(O0), .X1(X1));
endmodule
