// Logisim project ALU.circ as structural Verilog: 1 circuit, main circuit ALU
module ALU (
  input  A7,
  input  A6,
  input  A5,
  input  A4,
  input  A3,
  input  A2,
  input  A1,
  input  A0,
  input  S1,
  input  S0,
  input  B7,
  input  B6,
  input  B5,
  input  B4,
  input  B3,
  input  B2,
  input  B1,
  input  B0,
  output O0,
  output O1,
  output O2,
  output O3,
  output O4,
  output O5,
  output O6,
  output O7
);

  wire adder_subtractor_1_o0, adder_subtractor_1_o1, adder_subtractor_1_o2, adder_subtractor_1_o3,
       adder_subtractor_1_o4, adder_subtractor_1_o5, adder_subtractor_1_o6, adder_subtractor_1_o7, and_1_o0,
       and_1_o1, and_1_o2, and_1_o3, and_1_o4, and_1_o5, and_1_o6, and_1_o7, or_1_o0, or_1_o1, or_1_o2,
       or_1_o3, or_1_o4, or_1_o5, or_1_o6, or_1_o7;

  \and  and_1 (
    .O1(and_1_o1), .O0(and_1_o0), .O2(and_1_o2), .O3(and_1_o3), .O4(and_1_o4), .O5(and_1_o5), .O6(and_1_o6),
    .O7(and_1_o7), .A0(A0), .A1(A1), .A2(A2), .A3(A3), .A4(A4), .A5(A5), .A6(A6), .A7(A7), .B7(B7), .B6(B6),
    .B5(B5), .B4(B4), .B3(B3), .B2(B2), .B1(B1), .B0(B0));
  \or  or_1 (
    .O1(or_1_o1), .O0(or_1_o0), .O2(or_1_o2), .O3(or_1_o3), .O4(or_1_o4), .O5(or_1_o5), .O6(or_1_o6),
    .O7(or_1_o7), .A0(A0), .A1(A1), .A2(A2), .A3(A3), .A4(A4), .A5(A5), .A6(A6), .A7(A7), .B7(B7), .B6(B6),
    .B5(B5), .B4(B4), .B3(B3), .B2(B2), .B1(B1), .B0(B0));
  adder_subtractor adder_subtractor_1 (
    .S0(S0), .Y7(B7), .Y6(B6), .Y5(B5), .Y4(B4), .Y3(B3), .Y2(B2), .Y1(B1), .Y0(B0), .X7(A7), .X6(A6),
    .X5(A5), .X4(A4), .X3(A3), .X2(A2), .X1(A1), .X0(A0), .O0(adder_subtractor_1_o0),
    .O1(adder_subtractor_1_o1), .O2(adder_subtractor_1_o2), .O3(adder_subtractor_1_o3),
    .O4(adder_subtractor_1_o4), .O5(adder_subtractor_1_o5), .O6(adder_subtractor_1_o6),
    .O7(adder_subtractor_1_o7));
  multiplexor_2 multiplexor_2_1 (
    .S1(S1), .O0(O0), .O1(O1), .O2(O2), .O3(O3), .O4(O4), .O5(O5), .O6(O6), .O7(O7), .A7(and_1_o7),
    .A6(and_1_o6), .A5(and_1_o5), .A4(and_1_o4), .A3(and_1_o3), .A2(and_1_o2), .A1(and_1_o1), .A0(and_1_o0),
    .B7(or_1_o7), .B6(or_1_o6), .B5(or_1_o5), .B4(or_1_o4), .B3(or_1_o3), .B2(or_1_o2), .B1(or_1_o1),
    .B0(or_1_o0), .S0(S0), .C7(adder_subtractor_1_o7), .C6(adder_subtractor_1_o6),
    .C5(adder_subtractor_1_o5), .C4(adder_subtractor_1_o4), .C3(adder_subtractor_1_o3),
    .C2(adder_subtractor_1_o2), .C1(adder_subtractor_1_o1), .C0(adder_subtractor_1_o0),
    .D7(adder_subtractor_1_o7), .D6(adder_subtractor_1_o6), .D5(adder_subtractor_1_o5),
    .D4(adder_subtractor_1_o4), .D3(adder_subtractor_1_o3), .D2(adder_subtractor_1_o2),
    .D1(adder_subtractor_1_o1), .D0(adder_subtractor_1_o0));
endmodule
